// Logisim project expressao-1.circ as structural Verilog: 1 circuit, main circuit main
module main (
  input  A,
  input  B,
  input  C,
  output out_4
);

  wire and_1_out;

  and and_1 (and_1_out, A, B);
  or or_1 (out_4, and_1_out, C);
endmodule
